# Fritzing sketch Circuit schematic of IoT feeder (saved by Fritzing 0.9.3b)
breadboards: 1

parts:
  元件1 = Arduino Uno (Rev3)
  hc-sr1 = hc-sr04
  元件2 = OpenLog
  Load_Cell1 = Load Cell - Red/white/black/green
  MOTOR1 = 28BYJ-48 Stepper Motor
  ULN2003A_-_Stepper_Driver_Board1 = ULN2003A - Stepper Driver Board [package=board]
  J1 = Piezo Speaker

nets:
  N1: 元件1.D8, J1.pin2
  N2: 元件1.D10_PWM/SS, ULN2003A_-_Stepper_Driver_Board1.IN1
  N3: 元件1.D11_PWM/MOSI, ULN2003A_-_Stepper_Driver_Board1.IN2
  N4: 元件1.D12/MISO, ULN2003A_-_Stepper_Driver_Board1.IN3
  N5: 元件1.D13/SCK, ULN2003A_-_Stepper_Driver_Board1.IN4
  N6: 元件1.D3_PWM, hc-sr1.Trig
  N7: 元件1.D4, hc-sr1.Echo
  N8: 元件1.D6_PWM, 元件2.SCK
  N9: 元件1.D7, 元件2.MOSI
  VCC: 元件1.5V, hc-sr1.VCC, 元件2.MISO, ULN2003A_-_Stepper_Driver_Board1.VCC
  GND: 元件1.GND, hc-sr1.GND, 元件2.RST, ULN2003A_-_Stepper_Driver_Board1.GND, J1.pin1
  N10: 元件2.DTR, Load_Cell1.wire1
  N11: 元件2.RXI, Load_Cell1.wire3
  N12: 元件2.TXO, Load_Cell1.wire2
  N13: 元件2.VCC, Load_Cell1.wire4
  N14: MOTOR1.BLUE, ULN2003A_-_Stepper_Driver_Board1.BLUE, ULN2003A_-_Stepper_Driver_Board1.F
  N15: MOTOR1.PINK, ULN2003A_-_Stepper_Driver_Board1.PINK, ULN2003A_-_Stepper_Driver_Board1.E
  N16: MOTOR1.RED, ULN2003A_-_Stepper_Driver_Board1.RED, ULN2003A_-_Stepper_Driver_Board1.B
  N17: MOTOR1.ORANGE, ULN2003A_-_Stepper_Driver_Board1.ORANGE, ULN2003A_-_Stepper_Driver_Board1.C
  N18: MOTOR1.YELLOW, ULN2003A_-_Stepper_Driver_Board1.YELLOW, ULN2003A_-_Stepper_Driver_Board1.D

custom parts:
  Load Cell - Red/white/black/green: A rectangle load cell/weighting pressure Sensor with four wires - Red, white, black, green. Normally corresponding with E+, E-, A+, A- respectively.
  28BYJ-48 Stepper Motor: 28BYJ-48 gear-reduction stepper motor (small)
  ULN2003A - Stepper Driver Board: A common stepper motor driver board based on ULN2003APG darlington array
